// Logisim project Adder Circuits.circ as structural Verilog: 1 circuit, main circuit main
module main (
  input  in_1,
  input  in_2,
  input  in_3,
  input  in_4,
  input  in_5,
  output out_6,
  output out_7,
  output SUM,
  output out_9
);

  wire and_1_out, and_2_out, and_3_out, or_2_out, xor_1_out;

  xor xor_1 (xor_1_out, in_3, in_4);
  and and_1 (and_1_out, in_4, in_5);
  and and_2 (and_2_out, in_3, in_4);
  and and_3 (and_3_out, in_5, in_3);
  xor xor_2 (out_6, in_1, in_2);
  and and_4 (out_7, in_1, in_2);
  xor xor_3 (SUM, xor_1_out, in_5);
  or or_1 (out_9, and_1_out, or_2_out);
  or or_2 (or_2_out, and_2_out, and_3_out);

  // Notes on the sheet:
  //   HALF ADDER
  //   SUM
  //   CARRY
  //   FULL ADDER
  //   CARRY
endmodule
