// Logisim project Demultiplexor4Way.circ as structural Verilog: 1 circuit, main circuit main
module main (
  input  in_1,
  input  in_2,
  input  in_3,
  output out_4,
  output out_5,
  output out_6,
  output out_7
);

  wire and_1_out, and_2_out, and_3_out, and_4_out, not_1_out, not_2_out;

  not not_1 (not_1_out, in_1);
  not not_2 (not_2_out, in_2);
  and and_1 (and_1_out, not_2_out, not_1_out);
  and and_2 (and_2_out, not_1_out, in_2);
  and and_3 (and_3_out, not_2_out, in_1);
  and and_4 (and_4_out, in_2, in_1);
  and and_5 (out_4, and_1_out, in_3);
  and and_6 (out_5, and_2_out, in_3);
  and and_7 (out_6, in_3, and_3_out);
  and and_8 (out_7, in_3, and_4_out);
endmodule
