// Logisim project Full Adder.circ as structural Verilog: 1 circuit, main circuit main
module main (
  input  in_1,
  input  SUM_TOTAL,
  input  in_3,
  input  in_4,
  input  in_5,
  input  [3:0] in_6,
  input  [3:0] in_7,
  input  in_8,
  input  in_9,
  input  in_10,
  input  in_11,
  input  in_12,
  input  in_13,
  output [3:0] out_14,
  output out_15,
  output out_16,
  output out_17,
  output out_18,
  output out_19,
  output out_20
);

  wire and_1_out, and_2_out, and_3_out, and_4_out, and_5_out, and_6_out, and_7_out, and_8_out, and_9_out,
       and_10_out, or_1_out, or_2_out, or_3_out, or_4_out, or_5_out, or_6_out, xor_2_out, xor_4_out,
       xor_6_out;

  xor xor_1 (out_19, in_4, in_11);
  and and_1 (and_1_out, in_4, in_11);
  nand nand_1 (out_20, in_12, in_13);
  xor xor_2 (xor_2_out, and_1_out, in_3);
  and and_2 (and_2_out, in_3, in_10);
  and and_3 (and_3_out, and_1_out, in_3);
  and and_4 (and_4_out, in_10, and_1_out);
  xor xor_3 (out_18, xor_2_out, in_10);
  or or_1 (or_1_out, and_3_out, and_4_out);
  or or_2 (or_2_out, and_2_out, or_1_out);
  Adder #(.width(4)) adder_1 (.a(in_6), .b(in_7), .out(out_14), .cin(in_5), .cout(out_15));
  xor xor_4 (xor_4_out, or_2_out, SUM_TOTAL);
  and and_5 (and_5_out, SUM_TOTAL, in_9);
  and and_6 (and_6_out, or_2_out, SUM_TOTAL);
  and and_7 (and_7_out, in_9, or_2_out);
  xor xor_5 (out_17, xor_4_out, in_9);
  or or_3 (or_3_out, and_6_out, and_7_out);
  or or_4 (or_4_out, and_5_out, or_3_out);
  xor xor_6 (xor_6_out, or_4_out, in_1);
  and and_8 (and_8_out, in_1, in_8);
  and and_9 (and_9_out, or_4_out, in_1);
  and and_10 (and_10_out, in_8, or_4_out);
  xor xor_7 (out_16, xor_6_out, in_8);
  or or_5 (or_5_out, and_8_out, or_6_out);
  or or_6 (or_6_out, and_9_out, and_10_out);

  // Notes on the sheet:
  //   SUM
  //   CARRY
  //   SUM
  //   CARRY
  //   SUM
  //   CARRY
  //   SUM
  //   CARRY
endmodule
