// Logisim project Plexer.circ as structural Verilog: 1 circuit, main circuit main
module main (
  input  in_1,
  input  in_2,
  input  in_3,
  input  in_4,
  input  in_5,
  output out_6,
  output out_7,
  output out_8
);

  wire and_1_out, and_2_out, not_1_out, not_2_out;

  not not_1 (not_1_out, in_1);
  and and_1 (and_1_out, not_1_out, in_2);
  and and_2 (and_2_out, in_3, in_1);
  not not_2 (not_2_out, in_5);
  and and_3 (out_7, not_2_out, in_4);
  and and_4 (out_8, in_4, in_5);
  or or_1 (out_6, and_1_out, and_2_out);

  // Notes on the sheet:
  //   Multiplexer (MUX)
  //   Demultiplexer (DMUX)
endmodule
