// Logisim project sr_latch.circ as structural Verilog: 5 circuits, main circuit main
module main (
  output Q,
  output Q2
);

  wire R_out, S_out;

  Button S (.out(S_out));
  Button R (.out(R_out));
  nor nor_1 (Q, S_out, Q2);
  nor nor_2 (Q2, Q, R_out);

  // Notes on the sheet:
  //   SR Latch
endmodule

module d_latch (
  input  Set,
  input  Enable,
  output Q
);

  wire and_1_out, and_2_out, nor_2_out, not_1_out;

  not not_1 (not_1_out, Set);
  and and_1 (and_1_out, not_1_out, Enable);
  and and_2 (and_2_out, Enable, Set);
  nor nor_1 (Q, and_1_out, nor_2_out);
  nor nor_2 (nor_2_out, Q, and_2_out);

  // Notes on the sheet:
  //   D Latch
endmodule

module eightregh (
  input  [7:0] inp,
  input  load,
  output [7:0] out_3
);

  d_latch d_latch_1 (.Set(inp[0]), .Enable(load), .Q(out_3[0]));
  d_latch d_latch_2 (.Set(inp[1]), .Enable(load), .Q(out_3[1]));
  d_latch d_latch_3 (.Set(inp[2]), .Enable(load), .Q(out_3[2]));
  d_latch d_latch_4 (.Set(inp[3]), .Enable(load), .Q(out_3[3]));
  d_latch d_latch_5 (.Set(inp[4]), .Enable(load), .Q(out_3[4]));
  d_latch d_latch_6 (.Set(inp[5]), .Enable(load), .Q(out_3[5]));
  d_latch d_latch_7 (.Set(inp[6]), .Enable(load), .Q(out_3[6]));
  d_latch d_latch_8 (.Set(inp[7]), .Enable(load), .Q(out_3[7]));
endmodule

module eightram (
  input  [2:0] address,
  input  load,
  input  [7:0] iinp,
  output [7:0] data,
  output [7:0] data_1,
  output [7:0] data_2,
  output [7:0] data_3,
  output [7:0] data_4,
  output [7:0] data_5,
  output [7:0] data_6,
  output [7:0] data_7
);

  wire and_1_out, and_2_out, and_3_out, and_4_out, and_5_out, and_6_out, and_7_out, and_8_out, not_1_out,
       not_2_out, not_3_out;

  not not_1 (not_1_out, address[2]);
  not not_2 (not_2_out, address[1]);
  not not_3 (not_3_out, address[0]);
  and and_1 (and_1_out, not_3_out, load, not_2_out, not_1_out);
  LED led_1 (.in(and_1_out));
  and and_2 (and_2_out, address[0], load, not_2_out, not_1_out);
  LED led_2 (.in(and_2_out));
  and and_3 (and_3_out, not_3_out, load, address[1], not_1_out);
  LED led_3 (.in(and_3_out));
  and and_4 (and_4_out, address[0], load, address[1], not_1_out);
  LED led_4 (.in(and_4_out));
  and and_5 (and_5_out, not_3_out, load, not_2_out, address[2]);
  LED led_5 (.in(and_5_out));
  and and_6 (and_6_out, address[0], load, not_2_out, address[2]);
  LED led_6 (.in(and_6_out));
  and and_7 (and_7_out, not_3_out, load, address[1], address[2]);
  LED led_7 (.in(and_7_out));
  and and_8 (and_8_out, address[0], load, address[1], address[2]);
  LED led_8 (.in(and_8_out));
  eightregh eightregh_1 (.inp(iinp), .load(and_1_out), .out_3(data));
  eightregh eightregh_2 (.inp(iinp), .load(and_2_out), .out_3(data_1));
  eightregh eightregh_3 (.inp(iinp), .load(and_3_out), .out_3(data_2));
  eightregh eightregh_4 (.inp(iinp), .load(and_4_out), .out_3(data_3));
  eightregh eightregh_5 (.inp(iinp), .load(and_5_out), .out_3(data_4));
  eightregh eightregh_6 (.inp(iinp), .load(and_6_out), .out_3(data_5));
  eightregh eightregh_7 (.inp(iinp), .load(and_7_out), .out_3(data_6));
  eightregh eightregh_8 (.inp(iinp), .load(and_8_out), .out_3(data_7));
endmodule

module sixtyfourram (
  input  [5:0] address,
  input  load,
  input  [7:0] inp,
  output [7:0] data,
  output [7:0] data_1,
  output [7:0] data_2,
  output [7:0] data_3,
  output [7:0] data_4,
  output [7:0] data_5,
  output [7:0] data_6,
  output [7:0] data_7,
  output [7:0] data_8,
  output [7:0] data_9,
  output [7:0] data_10,
  output [7:0] data_11,
  output [7:0] data_12,
  output [7:0] data_13,
  output [7:0] data_14,
  output [7:0] data_15,
  output [7:0] data_16,
  output [7:0] data_17,
  output [7:0] data_18,
  output [7:0] data_19,
  output [7:0] data_20,
  output [7:0] data_21,
  output [7:0] data_22,
  output [7:0] data_23,
  output [7:0] data_24,
  output [7:0] data_25,
  output [7:0] data_26,
  output [7:0] data_27,
  output [7:0] data_28,
  output [7:0] data_29,
  output [7:0] data_30,
  output [7:0] data_31,
  output [7:0] data_32,
  output [7:0] data_33,
  output [7:0] data_34,
  output [7:0] data_35,
  output [7:0] data_36,
  output [7:0] data_37,
  output [7:0] data_38,
  output [7:0] data_39,
  output [7:0] data_40,
  output [7:0] data_41,
  output [7:0] data_42,
  output [7:0] data_43,
  output [7:0] data_44,
  output [7:0] data_45,
  output [7:0] data_46,
  output [7:0] data_47,
  output [7:0] data_48,
  output [7:0] data_49,
  output [7:0] data_50,
  output [7:0] data_51,
  output [7:0] data_52,
  output [7:0] data_53,
  output [7:0] data_54,
  output [7:0] data_55,
  output [7:0] data_56,
  output [7:0] data_57,
  output [7:0] data_58,
  output [7:0] data_59,
  output [7:0] data_60,
  output [7:0] data_61,
  output [7:0] data_62,
  output [7:0] data_63
);

  wire and_1_out, and_2_out, and_3_out, and_4_out, and_5_out, and_6_out, and_7_out, and_8_out, not_1_out,
       not_2_out, not_3_out;

  not not_1 (not_1_out, address[2]);
  not not_2 (not_2_out, address[1]);
  not not_3 (not_3_out, address[0]);
  and and_1 (and_1_out, load, not_3_out, not_2_out, not_1_out);
  and and_2 (and_2_out, load, not_3_out, not_2_out, address[2]);
  eightram eightram_1 (
    .address(address[5:3]), .load(and_1_out), .iinp(inp), .data(data), .data_1(data_4), .data_2(data_8),
    .data_3(data_12), .data_4(data_16), .data_5(data_20), .data_6(data_24), .data_7(data_28));
  eightram eightram_2 (
    .address(address[5:3]), .load(and_2_out), .iinp(inp), .data(data_32), .data_1(data_36), .data_2(data_40),
    .data_3(data_44), .data_4(data_48), .data_5(data_52), .data_6(data_56), .data_7(data_60));
  and and_3 (and_3_out, load, address[0], not_2_out, not_1_out);
  and and_4 (and_4_out, load, address[0], not_2_out, address[2]);
  eightram eightram_3 (
    .address(address[5:3]), .load(and_3_out), .iinp(inp), .data(data_1), .data_1(data_5), .data_2(data_9),
    .data_3(data_13), .data_4(data_17), .data_5(data_21), .data_6(data_25), .data_7(data_29));
  eightram eightram_4 (
    .address(address[5:3]), .load(and_4_out), .iinp(inp), .data(data_33), .data_1(data_37), .data_2(data_41),
    .data_3(data_45), .data_4(data_49), .data_5(data_53), .data_6(data_57), .data_7(data_61));
  and and_5 (and_5_out, load, not_3_out, address[1], not_1_out);
  and and_6 (and_6_out, load, not_3_out, address[1], address[2]);
  eightram eightram_5 (
    .address(address[5:3]), .load(and_5_out), .iinp(inp), .data(data_2), .data_1(data_6), .data_2(data_10),
    .data_3(data_14), .data_4(data_18), .data_5(data_22), .data_6(data_26), .data_7(data_30));
  eightram eightram_6 (
    .address(address[5:3]), .load(and_6_out), .iinp(inp), .data(data_34), .data_1(data_38), .data_2(data_42),
    .data_3(data_46), .data_4(data_50), .data_5(data_54), .data_6(data_58), .data_7(data_62));
  and and_7 (and_7_out, load, address[0], address[1], not_1_out);
  and and_8 (and_8_out, load, address[0], address[1], address[2]);
  eightram eightram_7 (
    .address(address[5:3]), .load(and_7_out), .iinp(inp), .data(data_3), .data_1(data_7), .data_2(data_11),
    .data_3(data_15), .data_4(data_19), .data_5(data_23), .data_6(data_27), .data_7(data_31));
  eightram eightram_8 (
    .address(address[5:3]), .load(and_8_out), .iinp(inp), .data(data_35), .data_1(data_39), .data_2(data_43),
    .data_3(data_47), .data_4(data_51), .data_5(data_55), .data_6(data_59), .data_7(data_63));
endmodule
